# Fritzing sketch ESP32 Multi PN5180 (saved by Fritzing 0.9.3b)

parts:
  Part2 = PN5180-NFC
  M2 = ESP32S-HiLetgo [part_number=ESP32S-HiLetgo]
  Part3 = PN5180-NFC
  Part4 = PN5180-NFC
  Part5 = PN5180-NFC

nets:
  5V: Part2.5V, M2.VIN, Part3.5V, Part4.5V, Part5.5V
  3.3V: Part2.3.3V, M2.3.3, Part4.3.3V, Part5.3.3V
  N1: Part2.RST, M2.GPIO22
  N2: Part2.NSS, M2.GPIO21
  N3: Part2.MOSI, M2.GPIO23, Part3.MOSI, Part4.MOSI, Part5.MOSI
  N4: Part2.MISO, M2.GPIO19, Part3.MISO, Part4.MISO, Part5.MISO
  N5: Part2.SCK, M2.GPIO18, Part3.SCK, Part4.SCK, Part5.SCK
  N6: Part2.BUSY, M2.GPIO5
  GND: Part2.GND, M2.GND, Part3.GND, Part4.GND, Part5.GND
  N7: M2.GPIO32, Part5.RST
  N8: M2.GPIO33, Part5.NSS
  N9: M2.GPIO25, Part5.BUSY
  N10: M2.GPIO15, Part4.BUSY
  N11: M2.GPIO2, Part4.NSS
  N12: M2.GPIO0, Part4.RST
  N13: M2.GPIO4, Part3.BUSY
  N14: M2.GPIO16, Part3.NSS
  N15: M2.GPIO17, Part3.RST

custom parts:
  PN5180-NFC: RFID High Frequency IC card reader/writer based on the PN5180 chip from NXP.
  ESP32S-HiLetgo: HiLetgo ESP-WROOM-32 ESP32 ESP-32S Development Board 2.4GHz Dual-Mode WiFi + Bluetooth Dual Cores Microcontroller The ESP32 integrated with Antenna switches, RF Balun, power amplifiers, low-noise amplifiers, filters, and management modules, and the entire solution occupies the least area of PCB. 2.4 GHz Wi-Fi plus Bluetooth dual-mode chip, with TSMC Ultra-low power consumption 40nm technology,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
