# Fritzing sketch ESP32 PN5180 (saved by Fritzing 0.9.3b)

parts:
  Part2 = PN5180-NFC
  M2 = ESP32S-HiLetgo [part_number=ESP32S-HiLetgo]

nets:
  5V: Part2.5V, M2.VIN
  N1: Part2.3.3V, M2.3.3
  N2: Part2.RST, M2.GPIO17
  N3: Part2.NSS, M2.GPIO5
  N4: Part2.MOSI, M2.GPIO23
  N5: Part2.MISO, M2.GPIO39, M2.GPIO19
  N6: Part2.SCK, M2.GPIO18
  N7: Part2.BUSY, M2.GPIO16
  GND: Part2.GND, M2.GND

notes:
  Note that this is the wiring for a 38-pin ESP32 board, such as the HiLetGo or the NodeMCU ESP-32S. Other ESP32 dev boards have different pinouts - please check!
  5V - (Red) - VIn
  3.3V - (Orange) - 3.3V
  RST - (Brown) - GPIO17
  NSS - (White) - GPIO5
  MOSI - (Green) - GPIO23 VSPI_MOSI
  MISO - (Blue) - GPIO19 VSPI_MISO
  SCK - (Yellow) - GPIO18 VSPI_SCK
  BUSY- (Grey) - GPIO16
  GND - (Black) - GND

custom parts:
  PN5180-NFC: RFID High Frequency IC card reader/writer based on the PN5180 chip from NXP.
  ESP32S-HiLetgo: HiLetgo ESP-WROOM-32 ESP32 ESP-32S Development Board 2.4GHz Dual-Mode WiFi + Bluetooth Dual Cores Microcontroller The ESP32 integrated with Antenna switches, RF Balun, power amplifiers, low-noise amplifiers, filters, and management modules, and the entire solution occupies the least area of PCB. 2.4 GHz Wi-Fi plus Bluetooth dual-mode chip, with TSMC Ultra-low power consumption 40nm technology,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
